// Logisim project DEcoder.circ as structural Verilog: 1 circuit, main circuit main
module main (
  input  X,
  input  Y,
  input  Z
);

  wire and_1_out, and_2_out, and_3_out, and_4_out, and_5_out, and_6_out, and_7_out, and_8_out, not_1_out,
       not_2_out, not_3_out, or_1_out, or_2_out, or_3_out;

  not not_1 (not_1_out, X);
  not not_2 (not_2_out, Y);
  not not_3 (not_3_out, Z);
  and and_1 (and_1_out, not_1_out, not_2_out, not_3_out);
  and and_2 (and_2_out, not_1_out, not_2_out, Z);
  and and_3 (and_3_out, not_1_out, Y, not_3_out);
  and and_4 (and_4_out, not_1_out, Y, Z);
  and and_5 (and_5_out, X, not_2_out, not_3_out);
  and and_6 (and_6_out, X, not_2_out, Z);
  and and_7 (and_7_out, X, Y, not_3_out);
  and and_8 (and_8_out, X, Y, Z);
  or or_1 (or_1_out, and_1_out, and_3_out);
  or or_2 (or_2_out, and_2_out, and_1_out, and_4_out, and_5_out, and_7_out);
  or or_3 (or_3_out, and_1_out, and_3_out, and_6_out, and_8_out);
  _7_Segment_Display u_7_segment_display_1 (
    .g(or_3_out), .f(1'b1), .a(or_3_out), .b(or_1_out), .e(or_2_out), .d(or_3_out), .c(or_3_out), .dp(1'b1));

  // Notes on the sheet:
  //   Decoder
  //   dot
  //   a
  //   b
  //   g
  //   c
  //   d
  //   e
  //   f
endmodule
