// Logisim project MUX.circ as structural Verilog: 1 circuit, main circuit main
module main (
  input  x,
  input  y,
  input  z
);

  wire and_1_out, and_2_out, and_3_out, and_4_out, and_5_out, and_6_out, and_7_out, and_8_out, and_9_out,
       and_10_out, and_11_out, and_12_out, and_13_out, and_14_out, and_15_out, and_16_out, and_17_out,
       and_18_out, and_19_out, and_20_out, and_21_out, and_22_out, and_23_out, and_24_out, not_1_out,
       not_2_out, not_3_out, not_4_out, not_5_out, not_6_out, not_7_out, not_8_out, not_9_out, not_10_out,
       not_11_out, not_12_out, not_13_out, not_14_out, not_15_out, not_16_out, not_17_out, not_18_out,
       not_19_out, not_20_out, not_21_out, not_22_out, not_23_out, not_24_out, not_25_out, not_26_out,
       not_27_out, not_28_out, not_29_out, not_30_out, not_31_out, not_32_out, not_33_out, not_34_out,
       not_35_out, not_36_out, or_1_out, or_2_out, or_3_out;

  not not_1 (not_1_out, x);
  not not_2 (not_2_out, y);
  not not_3 (not_3_out, z);
  not not_4 (not_4_out, y);
  not not_5 (not_5_out, x);
  not not_6 (not_6_out, x);
  not not_7 (not_7_out, z);
  not not_8 (not_8_out, x);
  not not_9 (not_9_out, y);
  not not_10 (not_10_out, z);
  not not_11 (not_11_out, y);
  not not_12 (not_12_out, z);
  not not_13 (not_13_out, x);
  not not_14 (not_14_out, y);
  not not_15 (not_15_out, z);
  not not_16 (not_16_out, y);
  not not_17 (not_17_out, x);
  not not_18 (not_18_out, x);
  not not_19 (not_19_out, z);
  not not_20 (not_20_out, x);
  not not_21 (not_21_out, y);
  not not_22 (not_22_out, z);
  not not_23 (not_23_out, y);
  not not_24 (not_24_out, z);
  not not_25 (not_25_out, x);
  not not_26 (not_26_out, y);
  not not_27 (not_27_out, z);
  not not_28 (not_28_out, y);
  not not_29 (not_29_out, x);
  not not_30 (not_30_out, x);
  not not_31 (not_31_out, z);
  not not_32 (not_32_out, x);
  not not_33 (not_33_out, y);
  not not_34 (not_34_out, z);
  not not_35 (not_35_out, y);
  not not_36 (not_36_out, z);
  and and_1 (and_1_out, not_1_out, 1'b1, not_2_out, not_3_out);
  and and_2 (and_2_out, 1'b0, not_4_out, not_5_out, z);
  and and_3 (and_3_out, 1'b1, not_6_out, not_7_out, y);
  and and_4 (and_4_out, 1'b0, not_8_out, y, z);
  and and_5 (and_5_out, 1'b0, not_9_out, not_10_out, x);
  and and_6 (and_6_out, 1'b0, not_11_out, x, z);
  and and_7 (and_7_out, 1'b0, not_12_out, y, x);
  and and_8 (and_8_out, 1'b0, x, y, z);
  and and_9 (and_9_out, not_13_out, 1'b1, not_14_out, not_15_out);
  and and_10 (and_10_out, 1'b0, not_16_out, not_17_out, z);
  and and_11 (and_11_out, 1'b1, not_18_out, not_19_out, y);
  and and_12 (and_12_out, 1'b0, not_20_out, y, z);
  and and_13 (and_13_out, 1'b0, not_21_out, not_22_out, x);
  and and_14 (and_14_out, 1'b1, not_23_out, x, z);
  and and_15 (and_15_out, 1'b0, not_24_out, y, x);
  and and_16 (and_16_out, 1'b1, x, y, z);
  and and_17 (and_17_out, not_25_out, 1'b1, not_26_out, not_27_out);
  and and_18 (and_18_out, 1'b1, not_28_out, not_29_out, z);
  and and_19 (and_19_out, 1'b0, not_30_out, not_31_out, y);
  and and_20 (and_20_out, 1'b1, not_32_out, y, z);
  and and_21 (and_21_out, 1'b1, not_33_out, not_34_out, x);
  and and_22 (and_22_out, 1'b0, not_35_out, x, z);
  and and_23 (and_23_out, 1'b1, not_36_out, y, x);
  and and_24 (and_24_out, 1'b0, x, y, z);
  or or_1 (or_1_out, and_1_out, and_2_out, and_3_out, and_4_out, and_5_out, and_6_out, and_7_out, and_8_out);
  or or_2 (or_2_out, and_9_out, and_10_out, and_11_out, and_12_out, and_13_out, and_14_out, and_15_out, and_16_out);
  or or_3 (or_3_out, and_17_out, and_18_out, and_19_out, and_20_out, and_21_out, and_22_out, and_23_out, and_24_out);
  _7_Segment_Display u_7_segment_display_1 (
    .g(or_2_out), .f(1'b1), .a(or_2_out), .b(or_1_out), .e(or_3_out), .d(or_2_out), .c(or_2_out), .dp(1'b1));

  // Notes on the sheet:
  //   x
  //   y
  //   z
  //   MUX
  //   a
  //   f
  //   b
  //   g
  //   dot
  //   c
  //   d
  //   e
endmodule
