// Logisim project Universal Gates.circ as structural Verilog: 1 circuit, main circuit main
module main (
  input  x,
  input  y,
  input  z
);

  wire nand_1_out, nand_2_out, nand_3_out, nand_4_out, nand_5_out, nand_6_out, nand_7_out, nand_8_out,
       nand_9_out, nand_10_out, nand_11_out, nand_12_out, nand_13_out, nand_14_out, nand_15_out, nand_16_out;

  nand nand_1 (nand_1_out, x, x);
  nand nand_2 (nand_2_out, y, y);
  nand nand_3 (nand_3_out, z, z);
  nand nand_4 (nand_4_out, x, z);
  nand nand_5 (nand_5_out, nand_1_out, nand_3_out);
  nand nand_6 (nand_6_out, nand_1_out, nand_3_out);
  nand nand_7 (nand_7_out, nand_6_out, nand_6_out);
  nand nand_8 (nand_8_out, x, nand_3_out);
  nand nand_9 (nand_9_out, nand_1_out, z);
  nand nand_10 (nand_10_out, nand_1_out, nand_2_out);
  nand nand_11 (nand_11_out, nand_12_out, nand_12_out);
  nand nand_12 (nand_12_out, nand_4_out, nand_5_out);
  nand nand_13 (nand_13_out, nand_8_out, nand_9_out, nand_10_out);
  nand nand_14 (nand_14_out, nand_11_out, nand_11_out);
  nand nand_15 (nand_15_out, nand_13_out, nand_13_out);
  nand nand_16 (nand_16_out, nand_15_out, nand_15_out);
  _7_Segment_Display u_7_segment_display_1 (
    .g(nand_14_out), .f(1'b1), .a(nand_14_out), .b(nand_7_out), .e(nand_16_out), .d(nand_14_out),
    .c(nand_14_out), .dp(1'b1));

  // Notes on the sheet:
  //   Universal Gates
  //   a
  //   c
  //   f
  //   d
  //   e
  //   dot
  //   b
  //   g
endmodule
