// Logisim project Decode.circ as structural Verilog: 1 circuit, main circuit main
module main (
);

  wire and_1_out, and_2_out, and_3_out, and_4_out, and_5_out, and_6_out, and_7_out, and_8_out, and_9_out,
       and_10_out, clock_1_out, not_1_out, not_2_out, not_3_out, or_1_out, or_2_out, or_3_out, or_4_out,
       t_ff_1_q, t_ff_1_qn, t_ff_2_q, t_ff_2_qn, t_ff_3_q, t_ff_3_qn;

  not not_1 (not_1_out, t_ff_1_q);
  not not_2 (not_2_out, t_ff_2_q);
  not not_3 (not_3_out, t_ff_3_q);
  and and_1 (and_1_out, not_1_out, not_2_out, not_3_out);
  and and_2 (and_2_out, not_1_out, not_2_out, t_ff_3_q);
  and and_3 (and_3_out, not_1_out, t_ff_2_q, not_3_out);
  and and_4 (and_4_out, not_1_out, t_ff_2_q, t_ff_3_q);
  and and_5 (and_5_out, t_ff_1_q, not_2_out, not_3_out);
  and and_6 (and_6_out, t_ff_1_q, not_2_out, t_ff_3_q);
  and and_7 (and_7_out, t_ff_1_q, t_ff_2_q, not_3_out);
  and and_8 (and_8_out, t_ff_1_q, t_ff_2_q, t_ff_3_q);
  Clock clock_1 (.out(clock_1_out));
  or or_1 (or_1_out, and_1_out, and_3_out);
  or or_2 (or_2_out, and_2_out, and_1_out, and_4_out, and_5_out, and_7_out);
  and and_9 (and_9_out, t_ff_3_q, t_ff_2_q);
  or or_3 (or_3_out, and_1_out, and_3_out, and_6_out, and_8_out);
  T_Flip_Flop t_ff_1 (.clk(clock_1_out), .T(and_9_out), .Q(t_ff_1_q), .Qn(t_ff_1_qn));  // open: preset, reset, en
  and and_10 (and_10_out, t_ff_2_q, t_ff_1_qn);
  T_Flip_Flop t_ff_2 (.clk(clock_1_out), .T(t_ff_3_q), .Q(t_ff_2_q), .Qn(t_ff_2_qn));  // open: preset, reset, en
  or or_4 (or_4_out, t_ff_2_qn, and_10_out, t_ff_3_qn);
  _7_Segment_Display u_7_segment_display_1 (
    .g(or_3_out), .f(1'b1), .a(or_3_out), .b(or_1_out), .e(or_2_out), .d(or_3_out), .c(or_3_out), .dp(1'b1));
  T_Flip_Flop t_ff_3 (.clk(clock_1_out), .T(or_4_out), .Q(t_ff_3_q), .Qn(t_ff_3_qn));  // open: preset, reset, en

  // Notes on the sheet:
  //   X
  //   Y
  //   Z
  //   Decoder
  //   dot
  //   x
  //   y
  //   a
  //   b
  //   g
  //   c
  //   d
  //   e
  //   z
  //   f
endmodule
