// Logisim project Universal Gates.circ as structural Verilog: 1 circuit, main circuit main
module main (
);

  wire clock_1_out, nand_1_out, nand_2_out, nand_3_out, nand_4_out, nand_5_out, nand_6_out, nand_7_out,
       nand_8_out, nand_9_out, nand_10_out, nand_11_out, nand_12_out, nand_13_out, nand_14_out, nand_15_out,
       nand_16_out, nand_17_out, nand_18_out, nand_19_out, nand_20_out, nand_21_out, nand_22_out,
       nand_23_out, nand_24_out, t_ff_1_q, t_ff_1_qn, t_ff_2_q, t_ff_2_qn, t_ff_3_q, t_ff_3_qn;

  nand nand_1 (nand_1_out, t_ff_1_q, t_ff_1_q);
  nand nand_2 (nand_2_out, t_ff_2_q, t_ff_2_q);
  nand nand_3 (nand_3_out, t_ff_3_q, t_ff_3_q);
  nand nand_4 (nand_4_out, t_ff_1_q, t_ff_3_q);
  nand nand_5 (nand_5_out, nand_1_out, nand_3_out);
  nand nand_6 (nand_6_out, nand_1_out, nand_3_out);
  nand nand_7 (nand_7_out, nand_6_out, nand_6_out);
  nand nand_8 (nand_8_out, t_ff_1_q, nand_3_out);
  nand nand_9 (nand_9_out, nand_1_out, t_ff_3_q);
  nand nand_10 (nand_10_out, nand_1_out, nand_2_out);
  Clock clock_1 (.out(clock_1_out));
  nand nand_11 (nand_11_out, nand_12_out, nand_12_out);
  nand nand_12 (nand_12_out, nand_4_out, nand_5_out);
  nand nand_13 (nand_13_out, nand_8_out, nand_9_out, nand_10_out);
  nand nand_14 (nand_14_out, nand_11_out, nand_11_out);
  nand nand_15 (nand_15_out, nand_13_out, nand_13_out);
  nand nand_16 (nand_16_out, nand_18_out, nand_18_out);
  nand nand_17 (nand_17_out, nand_15_out, nand_15_out);
  nand nand_18 (nand_18_out, t_ff_3_q, t_ff_2_q);
  T_Flip_Flop t_ff_1 (.clk(clock_1_out), .T(nand_16_out), .Q(t_ff_1_q), .Qn(t_ff_1_qn));  // open: preset, reset, en
  nand nand_19 (nand_19_out, t_ff_1_qn, t_ff_2_q);
  nand nand_20 (nand_20_out, t_ff_2_qn, t_ff_2_qn);
  T_Flip_Flop t_ff_2 (.clk(clock_1_out), .T(t_ff_3_q), .Q(t_ff_2_q), .Qn(t_ff_2_qn));  // open: preset, reset, en
  nand nand_21 (nand_21_out, nand_19_out, nand_20_out);
  nand nand_22 (nand_22_out, nand_21_out, nand_21_out);
  nand nand_23 (nand_23_out, t_ff_3_qn, t_ff_3_qn);
  T_Flip_Flop t_ff_3 (.clk(clock_1_out), .T(nand_24_out), .Q(t_ff_3_q), .Qn(t_ff_3_qn));  // open: preset, reset, en
  nand nand_24 (nand_24_out, nand_22_out, nand_23_out);
  _7_Segment_Display u_7_segment_display_1 (
    .g(nand_14_out), .f(1'b1), .a(nand_14_out), .b(nand_7_out), .e(nand_17_out), .d(nand_14_out),
    .c(nand_14_out), .dp(1'b1));

  // Notes on the sheet:
  //   x
  //   y
  //   z
  //   Universal Gates
  //   a
  //   c
  //   x
  //   f
  //   d
  //   e
  //   dot
  //   y
  //   b
  //   g
  //   z
endmodule
